# Fritzing sketch jumpOmeter (saved by Fritzing 0.9.4)

parts:
  WeMos_D1_Mini1 = WeMos D1 Mini
  Grove1 = Grove OLED 128x96
  R1 = Resistor [tolerance=±5% resistance=1k package="2010 [SMD]"]
  R2 = Resistor [tolerance=±5% resistance=1.8k package="0603 [SMD]"]
  hc-sr1 = hc-sr04

nets:
  3V3: WeMos_D1_Mini1.3V3, Grove1.VCC
  5V: WeMos_D1_Mini1.5V, hc-sr1.VCC
  N1: WeMos_D1_Mini1.D1, Grove1.SCL
  N2: WeMos_D1_Mini1.D2, Grove1.SDA
  N3: WeMos_D1_Mini1.D6, hc-sr1.Trig
  N4: WeMos_D1_Mini1.D7, R1.Pin_1, R2.Pin_0
  GND: WeMos_D1_Mini1.G, Grove1.GND, R2.Pin_1, hc-sr1.GND
  N5: R1.Pin_0, hc-sr1.Echo
